// Logisim project CPU.circ as structural Verilog: 4 circuits, main circuit main
module main (
  input  in_1
);

  wire alu_1_overflow, alu_1_zero_flag, and_1_out, and_2_out, and_3_out, and_4_out, and_5_out, and_6_out,
       CLK, JMP, JMP_A_REG_SAVE, JMP_B_REG_SAVE, JMP_C, JMP_NZ, JMP_Z, not_3_out, not_4_out, NOT_ZERO_REG,
       ON_OFF, or_1_out, or_2_out, OUT_LABEL, OVER_REG, ZERO_REG;
  wire [1:0] multiplexer_2_out_2;
  wire [3:0] adder_1_out, register_6_q;
  wire [5:0] multiplexer_2_out;
  wire [6:0] dipswitch_1_p7, dipswitch_2_p7, dipswitch_3_p7, dipswitch_4_p7, dipswitch_5_p7, register_5_q,
       register_5_q_2, register_5_q_3, register_5_q_4, register_5_q_5, register_7_q, register_7_q_2,
       register_7_q_3, register_7_q_4, register_7_q_5, register_8_q, register_8_q_2, register_8_q_3,
       register_8_q_4, register_8_q_5, register_9_q, register_9_q_2, register_9_q_3, register_9_q_4,
       register_9_q_5, register_10_q, register_10_q_2, register_10_q_3, register_10_q_4, register_10_q_5,
       register_11_q, register_11_q_2, register_11_q_3, register_11_q_4, register_11_q_5, register_12_q,
       register_12_q_2, register_12_q_3, register_12_q_4, register_12_q_5, register_13_q, register_13_q_2,
       register_13_q_3, register_13_q_4, register_13_q_5, register_14_q, register_14_q_2, register_14_q_3,
       register_14_q_4, register_14_q_5, register_15_q, register_15_q_2, register_15_q_3, register_15_q_4,
       register_15_q_5, register_16_q, register_16_q_2, register_16_q_3, register_16_q_4, register_16_q_5,
       register_17_q, register_17_q_2, register_17_q_3, register_17_q_4, register_17_q_5, register_18_q,
       register_18_q_2, register_18_q_3, register_18_q_4, register_18_q_5, register_19_q, register_19_q_2,
       register_19_q_3, register_19_q_4, register_19_q_5, register_20_q, register_20_q_2, register_20_q_3,
       register_20_q_4, register_20_q_5;
  wire [7:0] alu_1_out_c, demultiplexer_1_out7, demultiplexer_1_out15, multiplexer_1_out, ram_1_dout,
       register_1_q;
  wire [11:0] OPCODE_MEM_data;
  wire [15:0] counter_1_q, MEM_ADDR, rom_1_data;
  wire [34:0] register_4_q, rom_2_data;

  and and_1 (and_1_out, JMP_NZ, NOT_ZERO_REG);
  or or_1 (or_1_out, JMP, and_1_out, and_2_out, and_3_out);
  and and_2 (and_2_out, JMP_Z, ZERO_REG);
  Clock clock_1 (.out(CLK));
  and and_3 (and_3_out, JMP_C, OVER_REG);
  Counter #(.max('hffff), .width(16)) counter_1 (
    .clr(ON_OFF), .load(or_1_out), .up(1'b1), .count(1'b1), .clk(and_4_out), .D(MEM_ADDR), .Q(counter_1_q));  // open: carry
  not not_1 (ON_OFF, in_1);
  and and_4 (and_4_out, in_1, CLK);
  ROM #(.addrWidth(16), .dataWidth(16)) rom_1 (.addr(counter_1_q), .data(rom_1_data));
  ROM #(.addrWidth(4), .dataWidth(19)) OPCODE_MEM (
    .addr(rom_1_data[15:12]),
    .data({OUT_LABEL, JMP_NZ, JMP_C, JMP_Z, JMP, JMP_B_REG_SAVE, JMP_A_REG_SAVE, OPCODE_MEM_data}));
  Register #(.trigger("falling")) register_1 (
    .D(alu_1_out_c), .clk(OPCODE_MEM_data[11]), .Q(register_1_q), .clr(ON_OFF));  // open: en
  Multiplexer #(.width(8)) multiplexer_1 (
    .in0(rom_1_data[7:0]), .in1(register_1_q), .out(multiplexer_1_out), .sel(OPCODE_MEM_data[10]));
  RAM #(.addrWidth(4), .asyncread("true"), .trigger("falling"), .\type ("nonvolatile")) ram_1 (
    .addr(rom_1_data[11:8]), .we(OPCODE_MEM_data[0]), .oe(OPCODE_MEM_data[1]), .clk(CLK), .din(alu_1_out_c),
    .dout(ram_1_dout));
  ALU alu_1 (
    .PASS_A(OPCODE_MEM_data[9]), .DO_XOR(OPCODE_MEM_data[2]), .DO_OR(OPCODE_MEM_data[3]),
    .NEG_B(OPCODE_MEM_data[4]), .NEG_A(OPCODE_MEM_data[5]), .CIN(OPCODE_MEM_data[6]),
    .DO_AND(OPCODE_MEM_data[7]), .ADD(OPCODE_MEM_data[8]), .A(multiplexer_1_out), .B(ram_1_dout),
    .OUT_C(alu_1_out_c), .ZERO_FLAG(alu_1_zero_flag), .OVERFLOW(alu_1_overflow));
  D_Flip_Flop u_OVER_REG (.D(alu_1_overflow), .clk(CLK), .Q(OVER_REG));  // open: Qn, preset, reset
  D_Flip_Flop u_ZERO_REG (.D(alu_1_zero_flag), .clk(CLK), .Q(ZERO_REG));  // open: Qn, preset, reset
  not not_2 (NOT_ZERO_REG, ZERO_REG);
  // Probe on ram_1_dout
  // Probe on {multiplexer_2_out_2, multiplexer_2_out}
  ROM #(.addrWidth(6), .dataWidth(35)) rom_2 (.addr(multiplexer_2_out), .data(rom_2_data));
  Register #(.trigger("high")) register_2 (.D(ram_1_dout), .clk(JMP_A_REG_SAVE), .Q(MEM_ADDR[7:0]));  // open: en, clr
  Register #(.trigger("high")) register_3 (.D(ram_1_dout), .clk(JMP_B_REG_SAVE), .Q(MEM_ADDR[15:8]));  // open: en, clr
  Multiplexer #(.width(8)) multiplexer_2 (
    .in0(ram_1_dout), .in1({8{1'b0}}), .out({multiplexer_2_out_2, multiplexer_2_out}), .sel(not_3_out));
  not not_3 (not_3_out, OUT_LABEL);
  // Probe on MEM_ADDR
  and and_5 (and_5_out, multiplexer_2_out_2[0], multiplexer_2_out_2[1]);
  not not_4 (not_4_out, multiplexer_2_out_2[1]);
  // DipSwitch #(.number(7)) dipswitch_1: pin names not known; wires that end beside it: dipswitch_1_p7[6], dipswitch_1_p7[5], dipswitch_1_p7[4], dipswitch_1_p7[3], dipswitch_1_p7[2], dipswitch_1_p7[1], dipswitch_1_p7[0]
  DotMatrix dotmatrix_1 (
    .col0(register_4_q[34:28]), .col1(register_4_q[27:21]), .col2(register_4_q[20:14]),
    .col3(register_4_q[13:7]), .col4(register_4_q[6:0]));
  DotMatrix dotmatrix_2 (
    .col0(register_7_q_5), .col1(register_7_q_4), .col2(register_7_q_3), .col3(register_7_q_2),
    .col4(register_7_q));
  DotMatrix dotmatrix_3 (
    .col0(register_5_q_5), .col1(register_5_q_4), .col2(register_5_q_3), .col3(register_5_q_2),
    .col4(register_5_q));
  DotMatrix dotmatrix_4 (
    .col0(register_8_q_5), .col1(register_8_q_4), .col2(register_8_q_3), .col3(register_8_q_2),
    .col4(register_8_q));
  Register #(.trigger("falling"), .width(35)) register_4 (
    .D(rom_2_data), .clk(demultiplexer_1_out7[7]), .Q(register_4_q), .clr(or_2_out));  // open: en
  Register #(.trigger("falling"), .width(35)) register_5 (
    .D(rom_2_data), .clk(demultiplexer_1_out15[7]),
    .Q({register_5_q_5, register_5_q_4, register_5_q_3, register_5_q_2, register_5_q}), .clr(or_2_out));  // open: en
  or or_2 (or_2_out, and_5_out, ON_OFF);
  and and_6 (and_6_out, multiplexer_2_out_2[0], not_4_out);
  Register #(.trigger("falling"), .width(4)) register_6 (
    .D(adder_1_out), .clk(and_6_out), .Q(register_6_q), .clr(or_2_out));  // open: en
  // DipSwitch #(.number(7)) dipswitch_2: pin names not known; wires that end beside it: dipswitch_2_p7[6], dipswitch_2_p7[5], dipswitch_2_p7[4], dipswitch_2_p7[3], dipswitch_2_p7[2], dipswitch_2_p7[1], dipswitch_2_p7[0]
  DotMatrix dotmatrix_5 (
    .col0(register_9_q_5), .col1(register_9_q_4), .col2(register_9_q_3), .col3(register_9_q_2),
    .col4(register_9_q));
  DotMatrix dotmatrix_6 (
    .col0(register_10_q_5), .col1(register_10_q_4), .col2(register_10_q_3), .col3(register_10_q_2),
    .col4(register_10_q));
  Register #(.trigger("falling"), .width(35)) register_7 (
    .D(rom_2_data), .clk(demultiplexer_1_out7[6]),
    .Q({register_7_q_5, register_7_q_4, register_7_q_3, register_7_q_2, register_7_q}), .clr(or_2_out));  // open: en
  Register #(.trigger("falling"), .width(35)) register_8 (
    .D(rom_2_data), .clk(demultiplexer_1_out15[6]),
    .Q({register_8_q_5, register_8_q_4, register_8_q_3, register_8_q_2, register_8_q}), .clr(or_2_out));  // open: en
  Demultiplexer #(.select(4)) demultiplexer_1 (
    .out0(demultiplexer_1_out7[7]), .out1(demultiplexer_1_out7[6]), .out2(demultiplexer_1_out7[5]),
    .out3(demultiplexer_1_out7[4]), .out4(demultiplexer_1_out7[3]), .out5(demultiplexer_1_out7[2]),
    .out6(demultiplexer_1_out7[1]), .out7(demultiplexer_1_out7[0]), .out8(demultiplexer_1_out15[7]),
    .out9(demultiplexer_1_out15[6]), .out10(demultiplexer_1_out15[5]), .out11(demultiplexer_1_out15[4]),
    .out12(demultiplexer_1_out15[3]), .out13(demultiplexer_1_out15[2]), .out14(demultiplexer_1_out15[1]),
    .out15(demultiplexer_1_out15[0]), .in(and_6_out), .sel(register_6_q));
  // DipSwitch #(.number(7)) dipswitch_3: pin names not known; wires that end beside it: dipswitch_3_p7[6], dipswitch_3_p7[5], dipswitch_3_p7[4], dipswitch_3_p7[3], dipswitch_3_p7[2], dipswitch_3_p7[1], dipswitch_3_p7[0]
  DotMatrix dotmatrix_7 (
    .col0(register_11_q_5), .col1(register_11_q_4), .col2(register_11_q_3), .col3(register_11_q_2),
    .col4(register_11_q));
  DotMatrix dotmatrix_8 (
    .col0(register_12_q_5), .col1(register_12_q_4), .col2(register_12_q_3), .col3(register_12_q_2),
    .col4(register_12_q));
  Register #(.trigger("falling"), .width(35)) register_9 (
    .D(rom_2_data), .clk(demultiplexer_1_out7[5]),
    .Q({register_9_q_5, register_9_q_4, register_9_q_3, register_9_q_2, register_9_q}), .clr(or_2_out));  // open: en
  Register #(.trigger("falling"), .width(35)) register_10 (
    .D(rom_2_data), .clk(demultiplexer_1_out15[5]),
    .Q({register_10_q_5, register_10_q_4, register_10_q_3, register_10_q_2, register_10_q}), .clr(or_2_out));  // open: en
  Adder #(.width(4)) adder_1 (.a(register_6_q), .b(4'b0000), .out(adder_1_out), .cin(1'b1));  // open: cout
  // Probe on adder_1_out
  // DipSwitch #(.number(7)) dipswitch_4: pin names not known; wires that end beside it: dipswitch_4_p7[6], dipswitch_4_p7[5], dipswitch_4_p7[4], dipswitch_4_p7[3], dipswitch_4_p7[2], dipswitch_4_p7[1], dipswitch_4_p7[0]
  DotMatrix dotmatrix_9 (
    .col0(register_13_q_5), .col1(register_13_q_4), .col2(register_13_q_3), .col3(register_13_q_2),
    .col4(register_13_q));
  DotMatrix dotmatrix_10 (
    .col0(register_15_q_5), .col1(register_15_q_4), .col2(register_15_q_3), .col3(register_15_q_2),
    .col4(register_15_q));
  DotMatrix dotmatrix_11 (
    .col0(register_14_q_5), .col1(register_14_q_4), .col2(register_14_q_3), .col3(register_14_q_2),
    .col4(register_14_q));
  DotMatrix dotmatrix_12 (
    .col0(register_16_q_5), .col1(register_16_q_4), .col2(register_16_q_3), .col3(register_16_q_2),
    .col4(register_16_q));
  Register #(.trigger("falling"), .width(35)) register_11 (
    .D(rom_2_data), .clk(demultiplexer_1_out7[4]),
    .Q({register_11_q_5, register_11_q_4, register_11_q_3, register_11_q_2, register_11_q}), .clr(or_2_out));  // open: en
  Register #(.trigger("falling"), .width(35)) register_12 (
    .D(rom_2_data), .clk(demultiplexer_1_out15[4]),
    .Q({register_12_q_5, register_12_q_4, register_12_q_3, register_12_q_2, register_12_q}), .clr(or_2_out));  // open: en
  // DipSwitch #(.number(7)) dipswitch_5: pin names not known; wires that end beside it: dipswitch_5_p7[6], dipswitch_5_p7[5], dipswitch_5_p7[4], dipswitch_5_p7[3], dipswitch_5_p7[2], dipswitch_5_p7[1], dipswitch_5_p7[0]
  // Probe on {dipswitch_1_p7, dipswitch_2_p7, dipswitch_3_p7, dipswitch_4_p7, dipswitch_5_p7}
  DotMatrix dotmatrix_13 (
    .col0(register_17_q_5), .col1(register_17_q_4), .col2(register_17_q_3), .col3(register_17_q_2),
    .col4(register_17_q));
  DotMatrix dotmatrix_14 (
    .col0(register_18_q_5), .col1(register_18_q_4), .col2(register_18_q_3), .col3(register_18_q_2),
    .col4(register_18_q));
  Register #(.trigger("falling"), .width(35)) register_13 (
    .D(rom_2_data), .clk(demultiplexer_1_out7[3]),
    .Q({register_13_q_5, register_13_q_4, register_13_q_3, register_13_q_2, register_13_q}), .clr(or_2_out));  // open: en
  Register #(.trigger("falling"), .width(35)) register_14 (
    .D(rom_2_data), .clk(demultiplexer_1_out15[3]),
    .Q({register_14_q_5, register_14_q_4, register_14_q_3, register_14_q_2, register_14_q}), .clr(or_2_out));  // open: en
  DotMatrix dotmatrix_15 (
    .col0(register_19_q_5), .col1(register_19_q_4), .col2(register_19_q_3), .col3(register_19_q_2),
    .col4(register_19_q));
  DotMatrix dotmatrix_16 (
    .col0(register_20_q_5), .col1(register_20_q_4), .col2(register_20_q_3), .col3(register_20_q_2),
    .col4(register_20_q));
  Register #(.trigger("falling"), .width(35)) register_15 (
    .D(rom_2_data), .clk(demultiplexer_1_out7[2]),
    .Q({register_15_q_5, register_15_q_4, register_15_q_3, register_15_q_2, register_15_q}), .clr(or_2_out));  // open: en
  Register #(.trigger("falling"), .width(35)) register_16 (
    .D(rom_2_data), .clk(demultiplexer_1_out15[2]),
    .Q({register_16_q_5, register_16_q_4, register_16_q_3, register_16_q_2, register_16_q}), .clr(or_2_out));  // open: en
  Register #(.trigger("falling"), .width(35)) register_17 (
    .D(rom_2_data), .clk(demultiplexer_1_out7[1]),
    .Q({register_17_q_5, register_17_q_4, register_17_q_3, register_17_q_2, register_17_q}), .clr(or_2_out));  // open: en
  Register #(.trigger("falling"), .width(35)) register_18 (
    .D(rom_2_data), .clk(demultiplexer_1_out15[1]),
    .Q({register_18_q_5, register_18_q_4, register_18_q_3, register_18_q_2, register_18_q}), .clr(or_2_out));  // open: en
  Register #(.trigger("falling"), .width(35)) register_19 (
    .D(rom_2_data), .clk(demultiplexer_1_out7[0]),
    .Q({register_19_q_5, register_19_q_4, register_19_q_3, register_19_q_2, register_19_q}), .clr(or_2_out));  // open: en
  Register #(.trigger("falling"), .width(35)) register_20 (
    .D(rom_2_data), .clk(demultiplexer_1_out15[0]),
    .Q({register_20_q_5, register_20_q_4, register_20_q_3, register_20_q_2, register_20_q}), .clr(or_2_out));  // open: en

  // Notes on the sheet:
  //   contents of rom_1 (hex, n*v repeats v):
  //   0 6001 6101 6210 6e00 5000 1e40 8e00 5100 1000 6f04 af00 6d00 bd00 5100 7200 f000 6eff 8e00 6f01
  //   af00 6d00 bd00 c000
  //   PROGRAM_MEMORY
  //   contents of OPCODE_MEM (hex, n*v repeats v):
  //   200 501 481 409 405 80a 201 561 40002 0 1002 2002 4000 8000 10000 20000
  //   contents of rom_2 (hex, n*v repeats v):
  //   0 3f891223f 7f93264b6 3e83060a2 7f83060be 7f93264c1 7f9122440 3e83264ae 7f102047f 83fe080 202040fe
  //   7f3051141 fe04081 7f404107f 7f404067f 3e83060be 7f9122430 3e831613d 7f9132531 3293264a6 4081fe040
  //   7e02040fe 701c04770 7e02780fe 632820a63 60203c860 438b268e1 3ea3262be 43fc080 238b268a1 2283264b6
  //   78102047f 7993264c6 3e93264a6 40810207f 3693264b6 78912247f 1f4000 208136820 24*0 26205882
endmodule

module FullAdder (
  input  a,
  input  b,
  input  cin,
  output c,
  output cout
);

  wire and_1_out, and_2_out, and_3_out, and_4_out, and_5_out, and_6_out, and_7_out, not_1_out, not_2_out,
       not_3_out;

  not not_1 (not_1_out, a);
  not not_2 (not_2_out, b);
  not not_3 (not_3_out, cin);
  and and_1 (and_1_out, not_1_out, not_2_out, cin);
  and and_2 (and_2_out, not_1_out, b, not_3_out);
  and and_3 (and_3_out, a, not_2_out, not_3_out);
  and and_4 (and_4_out, a, b, cin);
  and and_5 (and_5_out, b, cin);
  and and_6 (and_6_out, a, cin);
  and and_7 (and_7_out, a, b);
  or or_1 (c, and_1_out, and_2_out, and_3_out, and_4_out);
  or or_2 (cout, and_5_out, and_6_out, and_7_out);
endmodule

module ALU (
  input  PASS_A,
  input  DO_XOR,
  input  DO_OR,
  input  NEG_B,
  input  NEG_A,
  input  CIN,
  input  DO_AND,
  input  ADD,
  input  [7:0] A,
  input  [7:0] B,
  output [7:0] OUT_C,
  output ZERO_FLAG,
  output OVERFLOW
);

  wire and_3_out, eightbitadder_1_cout;
  wire [2:0] priority_encoder_1_p5;
  wire [7:0] and_1_out, bit_extender_1_out, bit_extender_2_out, eightbitadder_1_out_4, or_1_out, xor_1_out,
       xor_2_out, xor_3_out;

  assign bit_extender_1_out = {{7{NEG_B}}, NEG_B};  // Bit_Extender bit_extender_1
  assign bit_extender_2_out = {{7{NEG_A}}, NEG_A};  // Bit_Extender bit_extender_2
  assign xor_1_out = bit_extender_2_out ^ A;  // XOR_Gate xor_1, 8 bits wide
  assign xor_2_out = B ^ bit_extender_1_out;  // XOR_Gate xor_2, 8 bits wide
  assign and_1_out = xor_1_out & xor_2_out;  // AND_Gate and_1, 8 bits wide
  assign or_1_out = xor_1_out | xor_2_out;  // OR_Gate or_1, 8 bits wide
  assign xor_3_out = xor_1_out ^ xor_2_out;  // XOR_Gate xor_3, 8 bits wide
  EightBitAdder eightbitadder_1 (
    .A(xor_1_out), .B(xor_2_out), .CIN(CIN), .out_4(eightbitadder_1_out_4), .COUT(eightbitadder_1_cout));
  and and_2 (OVERFLOW, eightbitadder_1_cout, ADD);
  // Priority_Encoder priority_encoder_1: pin names not known; wires that end beside it: ADD, DO_AND, DO_OR, DO_XOR, priority_encoder_1_p5, PASS_A, OUT_C[0], OUT_C[1], OUT_C[2], OUT_C[3], OUT_C[4], OUT_C[5], OUT_C[6], OUT_C[7]
  // Probe on priority_encoder_1_p5
  Multiplexer #(.select(3), .width(8)) multiplexer_1 (
    .in0(eightbitadder_1_out_4), .in1(and_1_out), .in2(or_1_out), .in3(xor_3_out), .in4(A), .out(OUT_C),
    .sel(priority_encoder_1_p5));  // open: in5, in6, in7
  and and_3 (and_3_out, ~OUT_C[0], ~OUT_C[1], ~OUT_C[2], ~OUT_C[3], ~OUT_C[4], ~OUT_C[5], ~OUT_C[6], ~OUT_C[7]);  // AND_Gate
  and and_4 (ZERO_FLAG, and_3_out, ADD);
endmodule

module EightBitAdder (
  input  [7:0] A,
  input  [7:0] B,
  input  CIN,
  output [7:0] out_4,
  output COUT
);

  wire fulladder_1_cout, fulladder_2_cout, fulladder_3_cout, fulladder_4_cout, fulladder_5_cout,
       fulladder_6_cout, fulladder_7_cout;

  // Probe on A
  // Probe on B
  FullAdder fulladder_1 (.a(A[0]), .b(B[0]), .cin(CIN), .c(out_4[0]), .cout(fulladder_1_cout));
  FullAdder fulladder_2 (.a(A[1]), .b(B[1]), .cin(fulladder_1_cout), .c(out_4[1]), .cout(fulladder_2_cout));
  FullAdder fulladder_3 (.a(A[2]), .b(B[2]), .cin(fulladder_2_cout), .c(out_4[2]), .cout(fulladder_3_cout));
  FullAdder fulladder_4 (.a(A[3]), .b(B[3]), .cin(fulladder_3_cout), .c(out_4[3]), .cout(fulladder_4_cout));
  FullAdder fulladder_5 (.a(A[4]), .b(B[4]), .cin(fulladder_4_cout), .c(out_4[4]), .cout(fulladder_5_cout));
  FullAdder fulladder_6 (.a(A[5]), .b(B[5]), .cin(fulladder_5_cout), .c(out_4[5]), .cout(fulladder_6_cout));
  FullAdder fulladder_7 (.a(A[6]), .b(B[6]), .cin(fulladder_6_cout), .c(out_4[6]), .cout(fulladder_7_cout));
  FullAdder fulladder_8 (.a(A[7]), .b(B[7]), .cin(fulladder_7_cout), .c(out_4[7]), .cout(COUT));
  // Probe on out_4
endmodule
